# Fritzing sketch Mendieta (saved by Fritzing 0.9.5d)
breadboards: 1

parts:
  Componente1 = Arduino Nano (Rev3.0)
  A1 = Orange pi zero lts
  U1 = Voltage Regulator - 5V [package="TO220 [THT]"]
  LCD1 = LCD screen
  M1 = DC Motor
  M2 = DC Motor
  L298N1 = L298N DC motor driver
  VCC1 = Battery
  LCM1602_IIC1 = LCM1602 IIC [part_number="LCM1602 IIC" chip_label="LCM1602 IIC" package="DIP (Dual Inline) [THT]"]
  HC-SR04_Sensor_1 = HC-SR04 Ultrasonic Distance Sensor
  M3 = fc-51 [package=THT]
  M4 = fc-51 [package=THT]
  M5 = fc-51 [package=THT]

nets:
  N1: Componente1.D5, L298N1.ENB
  N2: Componente1.D6, L298N1.IN4
  N3: Componente1.D7, L298N1.IN3
  N4: Componente1.D8, L298N1.IN2
  N5: Componente1.D9, L298N1.IN1
  N6: Componente1.D10, L298N1.ENA
  N7: Componente1.D11/MOSI, HC-SR04_Sensor_1.TRIG
  N8: Componente1.D12/MISO, HC-SR04_Sensor_1.ECHO
  N9: Componente1.A5, LCM1602_IIC1.SCL
  N10: Componente1.A4, LCM1602_IIC1.SDA
  N11: Componente1.A2, M5.pin1
  N12: Componente1.A1, M4.pin1
  N13: Componente1.A0, M3.pin1
  GND: A1.Pin_1, A1.Pin_5, A1.Pin_19, U1.GND, L298N1.GND, VCC1.-, LCM1602_IIC1.GND, HC-SR04_Sensor_1.GND, M3.pin2, M4.pin2, M5.pin2
  VCC: A1.Pin_4, A1.Pin_17, U1.output_voltage, L298N1.5V, LCM1602_IIC1.VCC, HC-SR04_Sensor_1.VCC, M3.pin3, M4.pin3, M5.pin3
  N14: U1.input_voltage, L298N1.12V, VCC1.+
  VSS: LCD1.VSS, LCM1602_IIC1.VSS
  VDD: LCD1.VDD, LCM1602_IIC1.VDD
  N15: LCD1.V0, LCM1602_IIC1.V0
  N16: LCD1.RS, LCM1602_IIC1.RS
  N17: LCD1.R/W, LCM1602_IIC1.RW
  N18: LCD1.E, LCM1602_IIC1.E
  N19: LCD1.DB0, LCM1602_IIC1.D0
  N20: LCD1.DB1, LCM1602_IIC1.D1
  N21: LCD1.DB2, LCM1602_IIC1.D2
  N22: LCD1.DB3, LCM1602_IIC1.D3
  N23: LCD1.DB4, LCM1602_IIC1.D4
  N24: LCD1.DB5, LCM1602_IIC1.D5
  N25: LCD1.DB6, LCM1602_IIC1.D6
  N26: LCD1.DB7, LCM1602_IIC1.D7
  N27: LCD1.LED+, LCM1602_IIC1.A
  N28: LCD1.LED-, LCM1602_IIC1.K
  N29: M1.pin_1, L298N1.OUT2
  N30: M1.pin_2, L298N1.OUT1
  N31: M2.pin_1, L298N1.OUT4
  N32: M2.pin_2, L298N1.OUT3

notes:
  7.4v --->
  5v --->
  LCD
  A4 A5
  Motores
  Der 10 9 8
  Izq 5 6 7
  Ultrasónico
  Trig 11
  Echo 12
  Sensores de línea
  A0 A1 A2
  El Nano se alimenta por USB desde la OPI
  NO cerrar el jumper regulador!
  Usar 4 pilas 14500
  (2 portapilas en paralelo)
  -----> 7.4V 3A
  O sólo 2 pilas 18650
  (1 solo portapilas)
  -----> 7.4V 2.6A

custom parts:
  Orange pi zero lts: Orange Pi Zero LTS is an open-source single-board computer. It can run Android 4.4, Ubuntu, Debian. It uses the AllWinner H2 SoC, and has 256MB/512MB DDR3 SDRAM(256MB version is Standard version), low running temperature and low power consumption.
  L298N DC motor driver: 2x DC motor driver with 78M05 positive voltage regulator (7..35 V) L298N: max 46 V, 2 A Set 5 V Enable jumper to enable 5 V regultor (needed for the L298N) and +5 V output at screw terminal or supply external +5 V at screw terminal Set ENA and/or ENB to +5 V to enable motor permanently or supply ENA and/or ENB with PWM signal IN1 and IN2 set rotation directory for motor A (OUT1/OUT2) IN2 and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
  LCM1602 IIC: I2C-Module to use a 1602 or 2004 LCD on with the wire.h libory Serial LCD Modul
